// Digital circuit 4bitMult.dig as structural Verilog
module _4bitMult (
  input  [3:0] A,
  input  [3:0] B,
  output [7:0] P
);

  wire adder_2_cout, adder_3_cout, adder_3_s, adder_4_cout, adder_5_cout, adder_5_s, adder_6_cout, adder_6_s,
       adder_7_cout, adder_7_s, adder_8_cout, adder_8_s, and_1_out, and_2_out, and_3_out, and_4_out,
       and_5_out, and_6_out, and_7_out, and_8_out, and_9_out, and_10_out, and_11_out, and_12_out, and_13_out,
       and_14_out, and_15_out, halfsum_1_cout, halfsum_1_s, halfsum_2_cout, halfsum_3_cout, halfsum_4_cout;

  and and_1 (and_1_out, A[3], B[3]);
  adder adder_1 (.A(and_1_out), .B(adder_2_cout), .Cin(adder_3_cout), .S(P[6]), .Cout(P[7]));
  and and_2 (and_2_out, A[2], B[3]);
  adder adder_2 (.A(adder_3_s), .B(and_2_out), .Cin(adder_4_cout), .S(P[5]), .Cout(adder_2_cout));
  and and_3 (and_3_out, A[3], B[2]);
  adder adder_3 (.A(adder_5_cout), .B(halfsum_1_cout), .Cin(and_3_out), .S(adder_3_s), .Cout(adder_3_cout));
  and and_4 (and_4_out, B[3], A[1]);
  adder adder_4 (.A(and_4_out), .B(adder_5_s), .Cin(halfsum_2_cout), .S(P[4]), .Cout(adder_4_cout));
  and and_5 (and_5_out, A[2], B[2]);
  adder adder_5 (.A(halfsum_1_s), .B(and_5_out), .Cin(adder_7_cout), .S(adder_5_s), .Cout(adder_5_cout));
  and and_6 (and_6_out, A[3], B[1]);
  halfSum halfsum_1 (.A(adder_6_cout), .B(and_6_out), .S(halfsum_1_s), .Cout(halfsum_1_cout));
  and and_7 (and_7_out, A[0], B[3]);
  and and_8 (and_8_out, A[1], B[2]);
  and and_9 (and_9_out, A[2], B[1]);
  halfSum halfsum_2 (.A(adder_7_s), .B(and_7_out), .S(P[3]), .Cout(halfsum_2_cout));
  and and_10 (and_10_out, A[3], B[0]);
  adder adder_6 (.A(and_10_out), .B(and_9_out), .Cin(adder_8_cout), .S(adder_6_s), .Cout(adder_6_cout));
  adder adder_7 (.A(adder_6_s), .B(and_8_out), .Cin(halfsum_4_cout), .S(adder_7_s), .Cout(adder_7_cout));
  and and_11 (and_11_out, A[1], B[1]);
  and and_12 (and_12_out, A[2], B[0]);
  adder adder_8 (.A(and_12_out), .B(and_11_out), .Cin(halfsum_3_cout), .S(adder_8_s), .Cout(adder_8_cout));
  and and_13 (and_13_out, A[0], B[1]);
  halfSum halfsum_3 (.A(and_15_out), .B(and_13_out), .S(P[1]), .Cout(halfsum_3_cout));
  and and_14 (and_14_out, A[0], B[2]);
  halfSum halfsum_4 (.A(and_14_out), .B(adder_8_s), .S(P[2]), .Cout(halfsum_4_cout));
  and and_15 (and_15_out, A[1], B[0]);
  and and_16 (P[0], A[0], B[0]);
  // Pins of 1 and 8 bits meet at P
endmodule
