// Digital circuit 8bitAdder.dig as structural Verilog
module _8bitAdder (
  input  [7:0] AC,
  input  [7:0] N,
  output [7:0] S,
  output [7:0] Cout
);

  wire add_1_c_o, add_2_c_o, add_3_c_o, add_4_c_o, add_5_c_o, add_6_c_o, add_7_c_o;

  Add add_1 (.a(AC[0]), .b(N[0]), .c_i(1'b0), .s(S[0]), .c_o(add_1_c_o));
  Add add_2 (.a(AC[1]), .b(N[1]), .c_i(add_1_c_o), .s(S[1]), .c_o(add_2_c_o));
  Add add_3 (.a(AC[2]), .b(N[2]), .c_i(add_2_c_o), .s(S[2]), .c_o(add_3_c_o));
  Add add_4 (.a(AC[3]), .b(N[3]), .c_i(add_3_c_o), .s(S[3]), .c_o(add_4_c_o));
  Add add_5 (.a(AC[4]), .b(N[4]), .c_i(add_4_c_o), .s(S[4]), .c_o(add_5_c_o));
  Add add_6 (.a(AC[5]), .b(N[5]), .c_i(add_5_c_o), .s(S[5]), .c_o(add_6_c_o));
  Add add_7 (.a(AC[6]), .b(N[6]), .c_i(add_6_c_o), .s(S[6]), .c_o(add_7_c_o));
  Add add_8 (.a(AC[7]), .b(N[7]), .c_i(add_7_c_o), .s(S[7]), .c_o(Cout[0]));
  // Pins of 1 and 8 bits meet at Cout
endmodule
