// Digital circuit 8bitDiv.dig as structural Verilog
module _8bitDiv (
  input  [7:0] N,
  input  [7:0] AC,
  output [7:0] R,
  output [7:0] Q
);

  wire [7:1] divcell_1_s, divcell_2_s, divcell_3_s, divcell_4_s, divcell_5_s, divcell_6_s, divcell_7_s;
  wire [7:7] divcell_1_s_2, divcell_2_s_2, divcell_3_s_2, divcell_4_s_2, divcell_5_s_2, divcell_6_s_2,
       divcell_7_s_2;

  DivCell divcell_1 (.A({{7{1'b0}}, AC[7]}), .B(N), .S({divcell_1_s_2[7], divcell_1_s}), .Qbit(Q[7]));
  DivCell divcell_2 (.A({divcell_1_s, AC[6]}), .B(N), .S({divcell_2_s_2[7], divcell_2_s}), .Qbit(Q[6]));
  DivCell divcell_3 (.A({divcell_2_s, AC[5]}), .B(N), .S({divcell_3_s_2[7], divcell_3_s}), .Qbit(Q[5]));
  DivCell divcell_4 (.A({divcell_3_s, AC[4]}), .B(N), .S({divcell_4_s_2[7], divcell_4_s}), .Qbit(Q[4]));
  DivCell divcell_5 (.A({divcell_4_s, AC[3]}), .B(N), .S({divcell_5_s_2[7], divcell_5_s}), .Qbit(Q[3]));
  DivCell divcell_6 (.A({divcell_5_s, AC[2]}), .B(N), .S({divcell_6_s_2[7], divcell_6_s}), .Qbit(Q[2]));
  DivCell divcell_7 (.A({divcell_6_s, AC[1]}), .B(N), .S({divcell_7_s_2[7], divcell_7_s}), .Qbit(Q[1]));
  DivCell divcell_8 (.A({divcell_7_s, AC[0]}), .B(N), .S(R), .Qbit(Q[0]));
endmodule
