// Digital circuit 8bitMult.dig as structural Verilog
module _8bitMult (
  input  [7:0] AC,
  input  [7:0] N,
  output [7:0] LSB,
  output [7:0] MSB
);

  wire _4bitadder_1_cout, _4bitadder_2_cout, _4bitadder_3_cout, _4bitadder_4_cout, _4bitadder_5_cout;
  wire [3:0] _4bitadder_1_s, _4bitadder_3_s, _4bitmult_1_p3, _4bitmult_2_p3, _4bitmult_2_p3_2,
       _4bitmult_3_p3, _4bitmult_3_p3_2, _4bitmult_4_p3, _4bitmult_4_p3_2;

  // _4bitMult _4bitmult_1: pin names not known; wires that end beside it: AC[3:0], N[3:0], {_4bitmult_1_p3, LSB[3:0]}
  // _4bitMult _4bitmult_2: pin names not known; wires that end beside it: AC[7:4], N[3:0], {_4bitmult_2_p3_2, _4bitmult_2_p3}
  // _4bitMult _4bitmult_3: pin names not known; wires that end beside it: AC[3:0], N[7:4], {_4bitmult_3_p3_2, _4bitmult_3_p3}
  // _4bitMult _4bitmult_4: pin names not known; wires that end beside it: N[7:4], AC[7:4], {_4bitmult_4_p3_2, _4bitmult_4_p3}
  _4bitadder _4bitadder_1 (
    .A(_4bitmult_1_p3), .B(_4bitmult_2_p3), .Cin(1'b0), .S(_4bitadder_1_s), .Cout(_4bitadder_1_cout));
  _4bitadder _4bitadder_2 (
    .A(_4bitadder_1_s), .B(_4bitmult_3_p3), .Cin(_4bitadder_1_cout), .S(LSB[7:4]), .Cout(_4bitadder_2_cout));
  _4bitadder _4bitadder_3 (
    .A(_4bitmult_2_p3_2), .B(_4bitmult_3_p3_2), .Cin(_4bitadder_2_cout), .S(_4bitadder_3_s),
    .Cout(_4bitadder_3_cout));
  _4bitadder _4bitadder_4 (
    .A(_4bitmult_4_p3), .B(_4bitadder_3_s), .Cin(_4bitadder_3_cout), .S(MSB[3:0]), .Cout(_4bitadder_4_cout));
  _4bitadder _4bitadder_5 (
    .A(_4bitmult_4_p3_2), .B(4'b0000), .Cin(_4bitadder_4_cout), .S(MSB[7:4]), .Cout(_4bitadder_5_cout));
  // also tied to GND on the sheet: _4bitadder_5_cout
endmodule
