// Digital circuit 8bitSub.dig as structural Verilog
module _8bitSub (
  input  [7:0] AC,
  input  [7:0] N,
  output [7:0] S,
  output Bout
);

  wire sub_1_p5, sub_2_p5, sub_3_p5, sub_4_p5, sub_5_p5, sub_6_p5, sub_7_p5;

  // Sub sub_1: pin names not known; wires that end beside it: AC[0], N[0], 1'b0, S[0], sub_1_p5
  // Sub sub_2: pin names not known; wires that end beside it: AC[1], N[1], sub_1_p5, S[1], sub_2_p5
  // Sub sub_3: pin names not known; wires that end beside it: AC[2], N[2], sub_2_p5, S[2], sub_3_p5
  // Sub sub_4: pin names not known; wires that end beside it: AC[3], N[3], sub_3_p5, S[3], sub_4_p5
  // Sub sub_5: pin names not known; wires that end beside it: AC[4], N[4], sub_4_p5, S[4], sub_5_p5
  // Sub sub_6: pin names not known; wires that end beside it: AC[5], N[5], sub_5_p5, S[5], sub_6_p5
  // Sub sub_7: pin names not known; wires that end beside it: AC[6], N[6], sub_6_p5, S[6], sub_7_p5
  // Sub sub_8: pin names not known; wires that end beside it: AC[7], N[7], sub_7_p5, S[7], Bout
endmodule
