// Digital circuit 8bitsNand.dig as structural Verilog
module _8bitsNand (
  input  [7:0] AC,
  input  [7:0] N,
  output [7:0] NAND
);

  assign NAND = ~(AC & N);  // NAnd nand_1, 8 bits wide
endmodule
