// Digital circuit ALU.dig as structural Verilog
module ALU (
  input  [7:0] N
);

  _8bitAdder _8bitadder_1 ();  // open: AC, N, S, Cout
  _8bitSub _8bitsub_1 ();  // open: AC, N, S, Bout
  _8bitMult _8bitmult_1 ();  // open: AC, N, LSB, MSB
  _8bitDiv _8bitdiv_1 ();  // open: N, AC, R, Q
  _8bitsShiftLeft _8bitsshiftleft_1 ();  // open: AC, L
  _8bitsShiftRight _8bitsshiftright_1 ();  // open: AC, R
  _8bitsXOR _8bitsxor_1 ();  // open: AC, N, X
  _8bitsNand _8bitsnand_1 ();  // open: AC, N, NAND
  Register #(.Bits(8)) register_1 (.D(N));  // open: C, en, Q
  Multiplexer #(.Bits(8), .Selector_Bits(3)) multiplexer_1 ();  // open: sel, in_0, in_1, in_2, in_3, in_4, in_5, in_6, in_7, out
endmodule
