// Digital circuit DivCell.dig as structural Verilog
module DivCell (
  input  [7:0] A,
  input  [7:0] B,
  output [7:0] S,
  output Qbit
);

  wire _8bitsub_1_bout;
  wire [7:0] _8bitsub_1_s;

  _8bitSub _8bitsub_1 (.AC(A), .N(B), .S(_8bitsub_1_s), .Bout(_8bitsub_1_bout));
  Multiplexer #(.Bits(8)) multiplexer_1 (.sel(_8bitsub_1_bout), .in_0(_8bitsub_1_s), .in_1(A), .out(S));
  not not_1 (Qbit, _8bitsub_1_bout);
endmodule
